// Logisim project CaioAndersonMartinsMoura-JoaoPedroPereiraFrutuoso-mips-datapath-PIPERLINE.circ as structural Verilog: 12 circuits, main circuit mips
module alu (
  input  [3:0] ALU_Control,
  input  [31:0] in_2,
  input  [31:0] in_3,
  output [31:0] out_4,
  output Zero
);

  wire comparator_1_lt;
  wire [31:0] adder_1_out, and_1_out, multiplexer_1_out, or_1_out, subtractor_1_out, xor_1_out;

  assign and_1_out = in_2 & in_3;  // AND_Gate and_1, 32 bits wide
  assign or_1_out = in_2 | in_3;  // OR_Gate or_1, 32 bits wide
  Adder #(.width(32)) adder_1 (.a(in_2), .b(in_3), .out(adder_1_out));  // open: cin, cout
  Subtractor #(.width(32)) subtractor_1 (.a(in_2), .b(in_3), .out(subtractor_1_out));  // open: bin, bout
  Comparator #(.width(32), .mode("unsigned")) comparator_1 (.a(in_2), .b(in_3), .lt(comparator_1_lt));  // open: gt, eq
  assign xor_1_out = in_2 ^ in_3;  // XOR_Gate xor_1, 32 bits wide
  Multiplexer #(.width(32), .enable("false")) multiplexer_1 (
    .in0({32{1'b0}}), .in1(32'h1), .out(multiplexer_1_out), .sel(comparator_1_lt));
  Multiplexer #(.select(4), .width(32), .disabled(0), .enable("false")) multiplexer_2 (
    .in0(and_1_out), .in1(or_1_out), .in2(adder_1_out), .in6(subtractor_1_out), .in7(multiplexer_1_out),
    .in12(xor_1_out), .out(out_4), .sel(ALU_Control));  // open: in3, in4, in5, in8, in9, in10, in11, in13, in14, in15
  Comparator #(.width(32), .mode("unsigned")) comparator_2 (.a(out_4), .b({32{1'b0}}), .eq(Zero));  // open: gt, lt

  // Notes on the sheet:
  //   A
  //   B
  //   Logic from the first table in Chapter 4.4
  //   Op selects the result
  //   Output
endmodule

module mips (
  input  [31:0] \INSTRUÇÃO 
);

  wire _0, alu_1_zero, Branch, C, JUMP, memread, memwrite, reg_ex_mem_1_out_11, reg_ex_mem_1_out_15,
       reg_id_ex_1_out_15, reg_mem_wb_1_out_8, regdst, regwrite, Zero_Reg_File_out;
  wire [1:0] ALUOP, control_1_aluop, control_1_regwrite, reg_ex_mem_1_out_10, reg_id_ex_1_out_12;
  wire [2:0] control_1_branch, reg_id_ex_1_out_13;
  wire [3:0] alu_control_1_operation, control_1_alusrc;
  wire [4:0] _1, _2, multiplexer_4_out, reg_ex_mem_1_out_18, reg_id_ex_1_out_21, reg_id_ex_1_out_22, writereg;
  wire [31:0] adder_1_out, alu_1_out_4, bit_extender_1_out, data, multiplexer_1_out, multiplexer_2_out,
       multiplexer_3_out, mux, PC_q, ram_1_data, reg_32_1_readdata1, reg_32_1_readdata2, reg_ex_mem_1_out_16,
       reg_ex_mem_1_out_17, reg_id_ex_1_out_18, reg_id_ex_1_out_19, reg_id_ex_1_out_20, reg_if_id_1_out_5,
       reg_if_id_1_out_6, reg_mem_wb_1_out_9, reg_mem_wb_1_out_10, rom_1_data, shifter_1_out, som, somadoleft;

  Register #(.width(32)) PC (.D(multiplexer_2_out), .Q(PC_q), .clk(C), .clr(_0));  // open: en
  Multiplexer #(.width(32), .enable("false")) multiplexer_1 (
    .in0(adder_1_out), .in1(mux), .out(multiplexer_1_out), .sel(Branch));
  Multiplexer #(.width(32), .enable("false")) multiplexer_2 (
    .in0(multiplexer_1_out), .in1({adder_1_out[31:28], rom_1_data[25:0], 2'b00}), .out(multiplexer_2_out),
    .sel(JUMP));
  Clock clock_1 (.out(C));
  Button Restart_Program (.out(_0));
  Button Zero_Reg_File (.out(Zero_Reg_File_out));
  Adder #(.width(32)) adder_1 (.a(PC_q), .b(32'h4), .out(adder_1_out));  // open: cin, cout
  // Probe on rom_1_data
  Reg_IF_ID reg_if_id_1 (
    .PC_4(adder_1_out), .IN_Instruction(rom_1_data), .out_5(reg_if_id_1_out_5),
    .out_6({reg_if_id_1_out_6[31:21], _2, _1, reg_if_id_1_out_6[10:0]}), .in_3(C), .in_4(_0));
  ROM #(.dataWidth(32)) rom_1 (.addr(PC_q[9:2]), .data(rom_1_data));  // open: sel
  Adder #(.width(32)) adder_2 (.a(shifter_1_out), .b(adder_1_out), .out(somadoleft));  // open: cin, cout
  Shifter #(.width(32)) shifter_1 (.in(som), .\dist (5'b00010), .out(shifter_1_out));
  control control_1 (
    .in_1(reg_if_id_1_out_6[31:26]), .RegDst(control_1_alusrc[3]), .Branch(control_1_branch[0]),
    .MemRead(control_1_branch[1]), .MemtoReg(control_1_regwrite[1]), .ALUOp(control_1_aluop),
    .MemWrite(control_1_branch[2]), .ALUSrc(control_1_alusrc[0]), .RegWrite(control_1_regwrite[0]),
    .JUMP(JUMP));
  reg_32 reg_32_1 (
    .ReadReg1(reg_if_id_1_out_6[25:21]), .ReadReg2(_2), .WriteReg(writereg), .RegWrite(regwrite),
    .ReadData1(reg_32_1_readdata1), .ReadData2(reg_32_1_readdata2), .WriteData(data), .Clk(C),
    .Reset(Zero_Reg_File_out));
  // Probe on reg_if_id_1_out_6[25:21]
  // Probe on _2
  // Probe on writereg
  assign bit_extender_1_out = {{16{_1[4]}}, {_1, reg_if_id_1_out_6[10:0]}};  // Bit_Extender bit_extender_1
  Reg_ID_EX reg_id_ex_1 (
    .RegWrite(control_1_regwrite), .MemtoReg(control_1_branch),
    .in_3({control_1_alusrc[3], control_1_aluop, control_1_alusrc[0]}), .PC_4(reg_if_id_1_out_5),
    .in_5(reg_32_1_readdata1), .in_6(reg_32_1_readdata2), .in_7(bit_extender_1_out), .in_8(_2), .in_9(_1),
    .out_12(reg_id_ex_1_out_12), .PC_4_2(som), .out_18(reg_id_ex_1_out_18), .out_19(reg_id_ex_1_out_19),
    .out_20(reg_id_ex_1_out_20), .out_21(reg_id_ex_1_out_21), .out_22(reg_id_ex_1_out_22), .in_10(C),
    .in_11(_0), .out_15(reg_id_ex_1_out_15), .RegDST(regdst), .out_13(reg_id_ex_1_out_13), .ALUOP(ALUOP));
  alu_control alu_control_1 (.Operation(alu_control_1_operation), .ALUOp(ALUOP), .Function(reg_id_ex_1_out_20[5:0]));
  alu alu_1 (
    .out_4(alu_1_out_4), .Zero(alu_1_zero), .in_2(reg_id_ex_1_out_18), .ALU_Control(alu_control_1_operation),
    .in_3(multiplexer_3_out));
  Multiplexer #(.width(32), .enable("false")) multiplexer_3 (
    .in0(reg_id_ex_1_out_19), .in1(reg_id_ex_1_out_20), .out(multiplexer_3_out), .sel(reg_id_ex_1_out_15));
  Multiplexer #(.width(5), .enable("false")) multiplexer_4 (
    .in0(reg_id_ex_1_out_21), .in1(reg_id_ex_1_out_22), .out(multiplexer_4_out), .sel(regdst));
  // Probe on alu_control_1_operation
  // Probe on adder_1_out
  Reg_EX_MEM reg_ex_mem_1 (
    .in_1(reg_id_ex_1_out_12), .in_2(reg_id_ex_1_out_13), .in_3(somadoleft), .in_5(alu_1_out_4),
    .in_6(reg_id_ex_1_out_19), .in_7(multiplexer_4_out), .out_10(reg_ex_mem_1_out_10), .out_14(mux),
    .out_16(reg_ex_mem_1_out_16), .out_17(reg_ex_mem_1_out_17), .out_18(reg_ex_mem_1_out_18), .in_8(C),
    .in_9(_0), .in_4(alu_1_zero), .out_15(reg_ex_mem_1_out_15), .out_11(reg_ex_mem_1_out_11),
    .out_12(memread), .out_13(memwrite));
  // Probe on reg_ex_mem_1_out_17
  and and_1 (Branch, reg_ex_mem_1_out_11, reg_ex_mem_1_out_15);
  RAM #(.dataWidth(32), .bus("separate")) ram_1 (
    .addr(reg_ex_mem_1_out_16[9:2]), .din(reg_ex_mem_1_out_17), .data(ram_1_data), .str(memwrite), .clk(C),
    .ld(memread));  // open: sel, clr
  Reg_MEM_WB reg_mem_wb_1 (
    .in_1(reg_ex_mem_1_out_10), .in_2(ram_1_data), .in_3(reg_ex_mem_1_out_16), .in_4(reg_ex_mem_1_out_18),
    .out_7(regwrite), .out_8(reg_mem_wb_1_out_8), .out_9(reg_mem_wb_1_out_9), .out_10(reg_mem_wb_1_out_10),
    .out_11(writereg), .in_5(C), .in_6(_0));
  Multiplexer #(.width(32), .enable("false")) multiplexer_5 (
    .in0(reg_mem_wb_1_out_10), .in1(reg_mem_wb_1_out_9), .out(data), .sel(reg_mem_wb_1_out_8));
  // Probe on writereg
  // Probe on data

  // Notes on the sheet:
  //   Your name and date: Caio Anderson M.M. & João Pedro Pereira Frutuoso
  //   Clock
  //   Current Instruction
  //   ALU Op
  //   Next PC
  //   Mem Addr
endmodule

module instruction_type_decode (
  input  [5:0] opcode,
  output R_format,
  output lw,
  output sw,
  output beq,
  output JUMP
);

  wire comparator_1_gt, comparator_1_lt;

  Comparator #(.width(6), .mode("unsigned")) comparator_1 (
    .a({6{1'b0}}), .b(opcode), .gt(comparator_1_gt), .eq(R_format), .lt(comparator_1_lt));
  Comparator #(.width(6), .mode("unsigned")) comparator_2 (.a(6'b100011), .b(opcode), .eq(lw));  // open: gt, lt
  Comparator #(.width(6), .mode("unsigned")) comparator_3 (.a(6'b101011), .b(opcode), .eq(sw));  // open: gt, lt
  Comparator #(.width(6), .mode("unsigned")) comparator_4 (.a(6'b000100), .b(opcode), .eq(beq));  // open: gt, lt
  Comparator #(.width(6), .mode("unsigned")) comparator_5 (.a(6'b000010), .b(opcode), .eq(JUMP));  // open: gt, lt

  // Notes on the sheet:
  //   This example sets "R-format" to true if opcode=00.
  //   ToDo: Fill in the logic from Fig 4.22 to determine the instruction type
  //   Hint: Use comparators and a constant to check for the right values
endmodule

module control_decode (
  input  Rformat,
  input  lw,
  input  sw,
  input  beq,
  output RegDst,
  output ALUSrc,
  output MemtoReg,
  output RegWrite,
  output MemRead,
  output MemWrite,
  output Branch,
  output ALUOp1,
  output ALUOp0
);

  or or_1 (ALUSrc, sw, lw);
  or or_2 (RegWrite, lw, Rformat);

  assign ALUOp0 = beq;
  assign ALUOp1 = Rformat;
  assign Branch = beq;
  assign MemRead = lw;
  assign MemtoReg = lw;
  assign MemWrite = sw;
  assign RegDst = Rformat;

  // Notes on the sheet:
  //   it into here.
endmodule

module alu_control (
  input  [5:0] Function,
  input  [1:0] ALUOp,
  output [3:0] Operation
);

  wire and_1_out, and_2_out, and_3_out, and_4_out, and_5_out, and_6_out, not_1_out, not_2_out, not_3_out,
       not_4_out, not_5_out, not_6_out, or_1_out, or_2_out;
  wire [2:0] priority_encoder_1_out;

  not not_1 (not_1_out, ALUOp[0]);
  not not_2 (not_2_out, ALUOp[1]);
  not not_3 (not_3_out, Function[3]);
  not not_4 (not_4_out, Function[2]);
  not not_5 (not_5_out, Function[1]);
  not not_6 (not_6_out, Function[0]);
  and and_1 (and_1_out, not_1_out, not_2_out);
  and and_2 (and_2_out, ~ALUOp[0], ALUOp[1], not_3_out, not_4_out, not_5_out, not_6_out);  // AND_Gate
  and and_3 (and_3_out, ALUOp[1], ~Function[3], ~Function[2], Function[1], ~Function[0]);  // AND_Gate
  and and_4 (and_4_out, ALUOp[1], ~Function[3], ~Function[1], Function[2], ~Function[0]);  // AND_Gate
  and and_5 (and_5_out, ALUOp[1], ~Function[3], Function[2], ~Function[1], Function[0]);  // AND_Gate
  and and_6 (and_6_out, ALUOp[1], Function[3], ~Function[2], Function[1], ~Function[0]);  // AND_Gate
  or or_1 (or_1_out, and_1_out, and_2_out);
  or or_2 (or_2_out, ALUOp[0], and_3_out);
  Priority_Encoder priority_encoder_1 (
    .in0(and_4_out), .in1(and_5_out), .in2(or_1_out), .in3(or_2_out), .in4(and_6_out),
    .out(priority_encoder_1_out));  // open: in5, in6, in7, en_in, gs, en_out
  Multiplexer #(.select(3), .width(4)) multiplexer_1 (
    .in0(4'b0000), .in1(4'b0001), .in2(4'b0010), .in3(4'b0110), .in4(4'b0111), .out(Operation),
    .sel(priority_encoder_1_out));  // open: in5, in6, in7, en

  // Notes on the sheet:
  //   Inputs
  //   B -- OR
  //   ToDo: Fill in logic from Fig 4.13
  //   Hint: Here is the logic for the first row: 
  //   A -- if (ALUOp1=0 and ALUOp0=0)
  //   D -- then output = 2 = 0010
  //   A
  //   C
  //   B
  //   C -- if (ALUOp1=1 and ALUOp0=0 and F3, F2, F1, F0 are all 0)
  //   B
  //   True for 0010=2
  //   True for 0110=6
  //   True for 0001=1
  //   True for 0111=7
  //   True for 0000=0
  //   We have 5 possible outputs
  //   D
  //   Depending on which input is 1,
  //   one of the outputs above will be selected.
endmodule

module control (
  input  [5:0] in_1,
  output RegDst,
  output Branch,
  output MemRead,
  output MemtoReg,
  output [1:0] ALUOp,
  output MemWrite,
  output ALUSrc,
  output RegWrite,
  output JUMP
);

  wire instruction_type_decode_1_beq, instruction_type_decode_1_lw, instruction_type_decode_1_r_format,
       instruction_type_decode_1_sw;

  instruction_type_decode instruction_type_decode_1 (
    .opcode(in_1), .R_format(instruction_type_decode_1_r_format), .lw(instruction_type_decode_1_lw),
    .sw(instruction_type_decode_1_sw), .beq(instruction_type_decode_1_beq), .JUMP(JUMP));
  control_decode control_decode_1 (
    .Rformat(instruction_type_decode_1_r_format), .RegDst(RegDst), .lw(instruction_type_decode_1_lw),
    .ALUSrc(ALUSrc), .MemtoReg(MemtoReg), .sw(instruction_type_decode_1_sw), .RegWrite(RegWrite),
    .beq(instruction_type_decode_1_beq), .MemRead(MemRead), .MemWrite(MemWrite), .Branch(Branch),
    .ALUOp1(ALUOp[1]), .ALUOp0(ALUOp[0]));

  // Notes on the sheet:
  //   Instruction OpCode
  //   Decode the Instruction Type first
  //   From the Insturction Type,
  //   decode the control signals
endmodule

module reg_32 (
  input  [4:0] ReadReg1,
  input  [4:0] ReadReg2,
  input  [4:0] WriteReg,
  input  RegWrite,
  input  [31:0] WriteData,
  input  Clk,
  input  Reset,
  output [31:0] ReadData1,
  output [31:0] ReadData2
);

  wire decoder_1_out0, decoder_1_out1, decoder_2_out0, decoder_2_out1, decoder_2_out2, decoder_2_out3,
       decoder_3_out0, decoder_3_out1, decoder_3_out2, decoder_3_out3, decoder_4_out0, decoder_4_out1,
       decoder_4_out2, decoder_4_out3, decoder_5_out0, decoder_5_out1, decoder_5_out2, decoder_5_out3,
       decoder_6_out0, decoder_6_out1, decoder_6_out2, decoder_6_out3, decoder_7_out0, decoder_7_out1,
       decoder_7_out2, decoder_7_out3, decoder_8_out0, decoder_8_out1, decoder_8_out2, decoder_8_out3,
       decoder_9_out0, decoder_9_out1, decoder_9_out2, decoder_9_out3, decoder_10_out0, decoder_10_out1,
       decoder_10_out2, decoder_10_out3, decoder_11_out0, decoder_11_out1, decoder_11_out2, decoder_11_out3;
  wire [31:0] multiplexer_1_out, multiplexer_2_out, multiplexer_3_out, multiplexer_4_out, multiplexer_5_out,
       multiplexer_6_out, multiplexer_7_out, multiplexer_8_out, multiplexer_9_out, multiplexer_10_out,
       multiplexer_13_out, multiplexer_14_out, multiplexer_15_out, multiplexer_16_out, multiplexer_17_out,
       multiplexer_18_out, multiplexer_19_out, multiplexer_20_out, multiplexer_21_out, multiplexer_22_out,
       register_1_q, register_2_q, register_3_q, register_4_q, register_5_q, register_6_q, register_7_q,
       register_8_q, register_9_q, register_10_q, register_11_q, register_12_q, register_13_q, register_14_q,
       register_15_q, register_16_q, register_17_q, register_18_q, register_19_q, register_20_q,
       register_21_q, register_22_q, register_23_q, register_24_q, register_25_q, register_26_q,
       register_27_q, register_28_q, register_29_q, register_30_q, register_31_q;

  // Probe on WriteReg
  Decoder #(.disabled(0)) decoder_1 (.out0(decoder_1_out0), .out1(decoder_1_out1), .sel(WriteReg[4]), .en(RegWrite));
  Decoder #(.select(2), .disabled(0)) decoder_2 (
    .out0(decoder_2_out0), .out1(decoder_2_out1), .out2(decoder_2_out2), .out3(decoder_2_out3),
    .sel(WriteReg[3:2]), .en(decoder_1_out0));
  Decoder #(.select(2), .disabled(0)) decoder_3 (
    .out0(decoder_3_out0), .out1(decoder_3_out1), .out2(decoder_3_out2), .out3(decoder_3_out3),
    .sel(WriteReg[1:0]), .en(decoder_2_out0));
  Decoder #(.select(2), .disabled(0)) decoder_4 (
    .out0(decoder_4_out0), .out1(decoder_4_out1), .out2(decoder_4_out2), .out3(decoder_4_out3),
    .sel(WriteReg[1:0]), .en(decoder_2_out1));
  Decoder #(.select(2), .disabled(0)) decoder_5 (
    .out0(decoder_5_out0), .out1(decoder_5_out1), .out2(decoder_5_out2), .out3(decoder_5_out3),
    .sel(WriteReg[1:0]), .en(decoder_2_out2));
  Decoder #(.select(2), .disabled(0)) decoder_6 (
    .out0(decoder_6_out0), .out1(decoder_6_out1), .out2(decoder_6_out2), .out3(decoder_6_out3),
    .sel(WriteReg[1:0]), .en(decoder_2_out3));
  Register #(.width(32)) register_1 (.D(WriteData), .en(decoder_3_out1), .Q(register_1_q), .clk(Clk), .clr(Reset));
  Register #(.width(32)) register_2 (.D(WriteData), .en(decoder_3_out2), .Q(register_2_q), .clk(Clk), .clr(Reset));
  Register #(.width(32)) register_3 (.D(WriteData), .en(decoder_3_out3), .Q(register_3_q), .clk(Clk), .clr(Reset));
  Register #(.width(32)) register_4 (.D(WriteData), .en(decoder_4_out0), .Q(register_4_q), .clk(Clk), .clr(Reset));
  Register #(.width(32)) register_5 (.D(WriteData), .en(decoder_4_out1), .Q(register_5_q), .clk(Clk), .clr(Reset));
  Register #(.width(32)) register_6 (.D(WriteData), .en(decoder_4_out2), .Q(register_6_q), .clk(Clk), .clr(Reset));
  Register #(.width(32)) register_7 (.D(WriteData), .en(decoder_4_out3), .Q(register_7_q), .clk(Clk), .clr(Reset));
  Register #(.width(32)) register_8 (.D(WriteData), .en(decoder_5_out0), .Q(register_8_q), .clk(Clk), .clr(Reset));
  Register #(.width(32)) register_9 (.D(WriteData), .en(decoder_5_out1), .Q(register_9_q), .clk(Clk), .clr(Reset));
  Register #(.width(32)) register_10 (.D(WriteData), .en(decoder_5_out2), .Q(register_10_q), .clk(Clk), .clr(Reset));
  Register #(.width(32)) register_11 (.D(WriteData), .en(decoder_5_out3), .Q(register_11_q), .clk(Clk), .clr(Reset));
  Register #(.width(32)) register_12 (.D(WriteData), .en(decoder_6_out0), .Q(register_12_q), .clk(Clk), .clr(Reset));
  Register #(.width(32)) register_13 (.D(WriteData), .en(decoder_6_out1), .Q(register_13_q), .clk(Clk), .clr(Reset));
  Register #(.width(32)) register_14 (.D(WriteData), .en(decoder_6_out2), .Q(register_14_q), .clk(Clk), .clr(Reset));
  Register #(.width(32)) register_15 (.D(WriteData), .en(decoder_6_out3), .Q(register_15_q), .clk(Clk), .clr(Reset));
  // Probe on {32{1'b0}}
  // Probe on register_1_q
  // Probe on register_2_q
  // Probe on register_3_q
  // Probe on register_4_q
  // Probe on register_5_q
  // Probe on register_6_q
  // Probe on register_7_q
  // Probe on register_8_q
  // Probe on register_9_q
  // Probe on register_10_q
  // Probe on register_11_q
  // Probe on register_12_q
  // Probe on register_13_q
  // Probe on register_14_q
  // Probe on register_15_q
  // Probe on ReadReg1
  Multiplexer #(.select(2), .width(32), .enable("false")) multiplexer_1 (
    .in0({32{1'b0}}), .in1(register_1_q), .in2(register_2_q), .in3(register_3_q), .out(multiplexer_1_out),
    .sel(ReadReg1[1:0]));
  Multiplexer #(.select(2), .width(32), .enable("false")) multiplexer_2 (
    .in0(register_4_q), .in1(register_5_q), .in2(register_6_q), .in3(register_7_q), .out(multiplexer_2_out),
    .sel(ReadReg1[1:0]));
  Multiplexer #(.select(2), .width(32), .enable("false")) multiplexer_3 (
    .in0(register_8_q), .in1(register_9_q), .in2(register_10_q), .in3(register_11_q),
    .out(multiplexer_3_out), .sel(ReadReg1[1:0]));
  Multiplexer #(.select(2), .width(32), .enable("false")) multiplexer_4 (
    .in0(register_12_q), .in1(register_13_q), .in2(register_14_q), .in3(register_15_q),
    .out(multiplexer_4_out), .sel(ReadReg1[1:0]));
  // Probe on ReadReg2
  Multiplexer #(.select(2), .width(32), .enable("false")) multiplexer_5 (
    .in0({32{1'b0}}), .in1(register_1_q), .in2(register_2_q), .in3(register_3_q), .out(multiplexer_5_out),
    .sel(ReadReg2[1:0]));
  Multiplexer #(.select(2), .width(32), .enable("false")) multiplexer_6 (
    .in0(register_4_q), .in1(register_5_q), .in2(register_6_q), .in3(register_7_q), .out(multiplexer_6_out),
    .sel(ReadReg2[1:0]));
  Multiplexer #(.select(2), .width(32), .enable("false")) multiplexer_7 (
    .in0(register_8_q), .in1(register_9_q), .in2(register_10_q), .in3(register_11_q),
    .out(multiplexer_7_out), .sel(ReadReg2[1:0]));
  Multiplexer #(.select(2), .width(32), .enable("false")) multiplexer_8 (
    .in0(register_12_q), .in1(register_13_q), .in2(register_14_q), .in3(register_15_q),
    .out(multiplexer_8_out), .sel(ReadReg2[1:0]));
  Multiplexer #(.select(2), .width(32), .enable("false")) multiplexer_9 (
    .in0(multiplexer_5_out), .in1(multiplexer_6_out), .in2(multiplexer_7_out), .in3(multiplexer_8_out),
    .out(multiplexer_9_out), .sel(ReadReg2[3:2]));
  Multiplexer #(.select(2), .width(32), .enable("false")) multiplexer_10 (
    .in0(multiplexer_1_out), .in1(multiplexer_2_out), .in2(multiplexer_3_out), .in3(multiplexer_4_out),
    .out(multiplexer_10_out), .sel(ReadReg1[3:2]));
  Decoder #(.select(2), .disabled(0)) decoder_7 (
    .out0(decoder_7_out0), .out1(decoder_7_out1), .out2(decoder_7_out2), .out3(decoder_7_out3),
    .sel(WriteReg[3:2]), .en(decoder_1_out1));
  Decoder #(.select(2), .disabled(0)) decoder_8 (
    .out0(decoder_8_out0), .out1(decoder_8_out1), .out2(decoder_8_out2), .out3(decoder_8_out3),
    .sel(WriteReg[1:0]), .en(decoder_7_out0));
  Decoder #(.select(2), .disabled(0)) decoder_9 (
    .out0(decoder_9_out0), .out1(decoder_9_out1), .out2(decoder_9_out2), .out3(decoder_9_out3),
    .sel(WriteReg[1:0]), .en(decoder_7_out1));
  Decoder #(.select(2), .disabled(0)) decoder_10 (
    .out0(decoder_10_out0), .out1(decoder_10_out1), .out2(decoder_10_out2), .out3(decoder_10_out3),
    .sel(WriteReg[1:0]), .en(decoder_7_out2));
  Decoder #(.select(2), .disabled(0)) decoder_11 (
    .out0(decoder_11_out0), .out1(decoder_11_out1), .out2(decoder_11_out2), .out3(decoder_11_out3),
    .sel(WriteReg[1:0]), .en(decoder_7_out3));
  Register #(.width(32)) register_16 (.D(WriteData), .en(decoder_8_out0), .Q(register_16_q), .clk(Clk), .clr(Reset));
  Register #(.width(32)) register_17 (.D(WriteData), .en(decoder_8_out1), .Q(register_17_q), .clk(Clk), .clr(Reset));
  Register #(.width(32)) register_18 (.D(WriteData), .en(decoder_8_out2), .Q(register_18_q), .clk(Clk), .clr(Reset));
  Register #(.width(32)) register_19 (.D(WriteData), .en(decoder_8_out3), .Q(register_19_q), .clk(Clk), .clr(Reset));
  Register #(.width(32)) register_20 (.D(WriteData), .en(decoder_9_out0), .Q(register_20_q), .clk(Clk), .clr(Reset));
  Register #(.width(32)) register_21 (.D(WriteData), .en(decoder_9_out1), .Q(register_21_q), .clk(Clk), .clr(Reset));
  Register #(.width(32)) register_22 (.D(WriteData), .en(decoder_9_out2), .Q(register_22_q), .clk(Clk), .clr(Reset));
  Register #(.width(32)) register_23 (.D(WriteData), .en(decoder_9_out3), .Q(register_23_q), .clk(Clk), .clr(Reset));
  Register #(.width(32)) register_24 (.D(WriteData), .en(decoder_10_out0), .Q(register_24_q), .clk(Clk), .clr(Reset));
  Register #(.width(32)) register_25 (.D(WriteData), .en(decoder_10_out1), .Q(register_25_q), .clk(Clk), .clr(Reset));
  Register #(.width(32)) register_26 (.D(WriteData), .en(decoder_10_out2), .Q(register_26_q), .clk(Clk), .clr(Reset));
  Register #(.width(32)) register_27 (.D(WriteData), .en(decoder_10_out3), .Q(register_27_q), .clk(Clk), .clr(Reset));
  Register #(.width(32)) register_28 (.D(WriteData), .en(decoder_11_out0), .Q(register_28_q), .clk(Clk), .clr(Reset));
  Register #(.width(32)) register_29 (.D(WriteData), .en(decoder_11_out1), .Q(register_29_q), .clk(Clk), .clr(Reset));
  Register #(.width(32)) register_30 (.D(WriteData), .en(decoder_11_out2), .Q(register_30_q), .clk(Clk), .clr(Reset));
  Register #(.width(32)) register_31 (.D(WriteData), .en(decoder_11_out3), .Q(register_31_q), .clk(Clk), .clr(Reset));
  // Probe on register_16_q
  // Probe on register_17_q
  // Probe on register_18_q
  // Probe on register_19_q
  // Probe on register_20_q
  // Probe on register_21_q
  // Probe on register_22_q
  // Probe on register_23_q
  // Probe on register_24_q
  // Probe on register_25_q
  // Probe on register_26_q
  // Probe on register_27_q
  // Probe on register_28_q
  // Probe on register_29_q
  // Probe on register_30_q
  // Probe on register_31_q
  Multiplexer #(.width(32), .enable("false")) multiplexer_11 (
    .in0(multiplexer_10_out), .in1(multiplexer_21_out), .out(ReadData1), .sel(ReadReg1[4]));
  Multiplexer #(.width(32), .enable("false")) multiplexer_12 (
    .in0(multiplexer_9_out), .in1(multiplexer_22_out), .out(ReadData2), .sel(ReadReg2[4]));
  Multiplexer #(.select(2), .width(32), .enable("false")) multiplexer_13 (
    .in0(register_16_q), .in1(register_17_q), .in2(register_18_q), .in3(register_19_q),
    .out(multiplexer_13_out), .sel(ReadReg1[1:0]));
  Multiplexer #(.select(2), .width(32), .enable("false")) multiplexer_14 (
    .in0(register_20_q), .in1(register_21_q), .in2(register_22_q), .in3(register_23_q),
    .out(multiplexer_14_out), .sel(ReadReg1[1:0]));
  Multiplexer #(.select(2), .width(32), .enable("false")) multiplexer_15 (
    .in0(register_24_q), .in1(register_25_q), .in2(register_26_q), .in3(register_27_q),
    .out(multiplexer_15_out), .sel(ReadReg1[1:0]));
  Multiplexer #(.select(2), .width(32), .enable("false")) multiplexer_16 (
    .in0(register_28_q), .in1(register_29_q), .in2(register_30_q), .in3(register_31_q),
    .out(multiplexer_16_out), .sel(ReadReg1[1:0]));
  Multiplexer #(.select(2), .width(32), .enable("false")) multiplexer_17 (
    .in0(register_16_q), .in1(register_17_q), .in2(register_18_q), .in3(register_19_q),
    .out(multiplexer_17_out), .sel(ReadReg2[1:0]));
  Multiplexer #(.select(2), .width(32), .enable("false")) multiplexer_18 (
    .in0(register_20_q), .in1(register_21_q), .in2(register_22_q), .in3(register_23_q),
    .out(multiplexer_18_out), .sel(ReadReg2[1:0]));
  Multiplexer #(.select(2), .width(32), .enable("false")) multiplexer_19 (
    .in0(register_24_q), .in1(register_25_q), .in2(register_26_q), .in3(register_27_q),
    .out(multiplexer_19_out), .sel(ReadReg2[1:0]));
  Multiplexer #(.select(2), .width(32), .enable("false")) multiplexer_20 (
    .in0(register_28_q), .in1(register_29_q), .in2(register_30_q), .in3(register_31_q),
    .out(multiplexer_20_out), .sel(ReadReg2[1:0]));
  Multiplexer #(.select(2), .width(32), .enable("false")) multiplexer_21 (
    .in0(multiplexer_17_out), .in1(multiplexer_18_out), .in2(multiplexer_19_out), .in3(multiplexer_20_out),
    .out(multiplexer_21_out), .sel(ReadReg2[3:2]));
  Multiplexer #(.select(2), .width(32), .enable("false")) multiplexer_22 (
    .in0(multiplexer_13_out), .in1(multiplexer_14_out), .in2(multiplexer_15_out), .in3(multiplexer_16_out),
    .out(multiplexer_22_out), .sel(ReadReg1[3:2]));

  // Notes on the sheet:
  //   $2 = $v0
  //   $3 = $v1
  //   $0 = $zero
  //   $8 = $t0
  //   $16 = $s0
endmodule

module Testes (
  input  in_1,
  input  [4:0] in_2,
  input  [4:0] in_3,
  input  [4:0] in_4,
  input  [31:0] in_5,
  input  [31:0] A,
  input  [31:0] B,
  input  [3:0] Alu_OP
);

  wire button_1_out, clock_1_out, undriven, undriven_2;
  wire [31:0] reg_32_1_readdata1, reg_32_1_readdata2;

  Clock clock_1 (.out(clock_1_out));
  Button button_1 (.out(button_1_out));
  // Probe on in_2
  // Probe on in_3
  // Probe on in_4
  // Probe on in_5
  reg_32 reg_32_1 (
    .ReadReg1(in_2), .ReadReg2(in_3), .WriteReg(in_4), .RegWrite(in_1), .ReadData1(reg_32_1_readdata1),
    .ReadData2(reg_32_1_readdata2), .WriteData(in_5), .Clk(clock_1_out), .Reset(button_1_out));
  // Probe on A
  // Probe on B
  // alu alu_1: pin names not known; wires that end beside it: A
  // Probe on reg_32_1_readdata1
  // Probe on reg_32_1_readdata2
  // Probe on undriven
  // Probe on undriven_2
endmodule

module Reg_IF_ID (
  input  [31:0] PC_4,
  input  [31:0] IN_Instruction,
  input  in_3,
  input  in_4,
  output [31:0] out_5,
  output [31:0] out_6
);

  Register #(.width(32)) register_1 (.D(PC_4), .Q(out_5), .clk(in_3), .clr(in_4));  // open: en
  Register #(.width(32)) register_2 (.D(IN_Instruction), .Q(out_6), .clk(in_3), .clr(in_4));  // open: en
endmodule

module Reg_ID_EX (
  input  [1:0] RegWrite,
  input  [2:0] MemtoReg,
  input  [3:0] in_3,
  input  [31:0] PC_4,
  input  [31:0] in_5,
  input  [31:0] in_6,
  input  [31:0] in_7,
  input  [4:0] in_8,
  input  [4:0] in_9,
  input  in_10,
  input  in_11,
  output [1:0] out_12,
  output [2:0] out_13,
  output [1:0] ALUOP,
  output out_15,
  output RegDST,
  output [31:0] PC_4_2,
  output [31:0] out_18,
  output [31:0] out_19,
  output [31:0] out_20,
  output [4:0] out_21,
  output [4:0] out_22
);

  Register #(.width(2)) register_1 (.D(RegWrite), .Q(out_12), .clk(in_10), .clr(in_11));  // open: en
  Register #(.width(3)) register_2 (.D(MemtoReg), .Q(out_13), .clk(in_10), .clr(in_11));  // open: en
  Register #(.width(4)) register_3 (.D(in_3), .Q({RegDST, ALUOP, out_15}), .clk(in_10), .clr(in_11));  // open: en
  Register #(.width(32)) register_4 (.D(PC_4), .Q(PC_4_2), .clk(in_10), .clr(in_11));  // open: en
  Register #(.width(32)) register_5 (.D(in_5), .Q(out_18), .clk(in_10), .clr(in_11));  // open: en
  Register #(.width(32)) register_6 (.D(in_6), .Q(out_19), .clk(in_10), .clr(in_11));  // open: en
  Register #(.width(32)) register_7 (.D(in_7), .Q(out_20), .clk(in_10), .clr(in_11));  // open: en
  Register #(.width(5)) register_8 (.D(in_8), .Q(out_21), .clk(in_10), .clr(in_11));  // open: en
  Register #(.width(5)) register_9 (.D(in_9), .Q(out_22), .clk(in_10), .clr(in_11));  // open: en
endmodule

module Reg_EX_MEM (
  input  [1:0] in_1,
  input  [2:0] in_2,
  input  [31:0] in_3,
  input  in_4,
  input  [31:0] in_5,
  input  [31:0] in_6,
  input  [4:0] in_7,
  input  in_8,
  input  in_9,
  output [1:0] out_10,
  output out_11,
  output out_12,
  output out_13,
  output [31:0] out_14,
  output out_15,
  output [31:0] out_16,
  output [31:0] out_17,
  output [4:0] out_18
);

  Register #(.width(2)) register_1 (.D(in_1), .Q(out_10), .clk(in_8), .clr(in_9));  // open: en
  Register #(.width(3)) register_2 (.D(in_2), .Q({out_13, out_12, out_11}), .clk(in_8), .clr(in_9));  // open: en
  Register #(.width(32)) register_3 (.D(in_3), .Q(out_14), .clk(in_8), .clr(in_9));  // open: en
  Register #(.width(1)) register_4 (.D(in_4), .Q(out_15), .clk(in_8), .clr(in_9));  // open: en
  Register #(.width(32)) register_5 (.D(in_5), .Q(out_16), .clk(in_8), .clr(in_9));  // open: en
  Register #(.width(32)) register_6 (.D(in_6), .Q(out_17), .clk(in_8), .clr(in_9));  // open: en
  Register #(.width(5)) register_7 (.D(in_7), .Q(out_18), .clk(in_8), .clr(in_9));  // open: en
endmodule

module Reg_MEM_WB (
  input  [1:0] in_1,
  input  [31:0] in_2,
  input  [31:0] in_3,
  input  [4:0] in_4,
  input  in_5,
  input  in_6,
  output out_7,
  output out_8,
  output [31:0] out_9,
  output [31:0] out_10,
  output [4:0] out_11
);

  Register #(.width(2)) register_1 (.D(in_1), .Q({out_8, out_7}), .clk(in_5), .clr(in_6));  // open: en
  Register #(.width(32)) register_2 (.D(in_2), .Q(out_9), .clk(in_5), .clr(in_6));  // open: en
  Register #(.width(32)) register_3 (.D(in_3), .Q(out_10), .clk(in_5), .clr(in_6));  // open: en
  Register #(.width(5)) register_4 (.D(in_4), .Q(out_11), .clk(in_5), .clr(in_6));  // open: en
endmodule
